// Logisim project 1.Name.circ as structural Verilog: 1 circuit, main circuit main
module main (
);

  DotMatrix #(.matrixcols(24), .matrixrows(24)) dotmatrix_1 (
    .col0({24{1'b0}}), .col1({24{1'b0}}), .col2(24'h4000), .col3(24'h4000), .col4(24'h8000),
    .col5(24'h1fffe), .col6(24'h70000), .col7(24'h1c0080), .col8(24'h80), .col9(24'h80080),
    .col10(24'hbfe80), .col11(24'ha4880), .col12(24'ha4880), .col13(24'ha4880), .col14(24'h7ffea0),
    .col15(24'ha4894), .col16(24'ha4886), .col17(24'h2a49fe), .col18(24'hbfe80), .col19(24'h80080),
    .col20(24'h80), .col21(24'h80), .col22({24{1'b0}}), .col23({24{1'b0}}));
  DotMatrix #(.matrixcols(24), .matrixrows(24)) dotmatrix_2 (
    .col0({24{1'b0}}), .col1({24{1'b0}}), .col2({24{1'b0}}), .col3({24{1'b0}}), .col4({24{1'b0}}),
    .col5({24{1'b0}}), .col6({24{1'b0}}), .col7(24'h3fe00), .col8(24'h22200), .col9(24'h22200),
    .col10(24'h22200), .col11(24'h3ffff8), .col12(24'h22200), .col13(24'h22200), .col14(24'h22200),
    .col15(24'h3fe00), .col16({24{1'b0}}), .col17({24{1'b0}}), .col18({24{1'b0}}), .col19({24{1'b0}}),
    .col20({24{1'b0}}), .col21({24{1'b0}}), .col22({24{1'b0}}), .col23({24{1'b0}}));
endmodule
