// Logisim project 3.MOS.circ as structural Verilog: 8 circuits, main circuit And Gate
module And_Gate (
  input  in_1,
  input  in_2,
  output out_3
);

  wire transistor_2_out;

  Transistor transistor_1 (.in(1'b0), .out(out_3), .gate(in_2));
  Transistor #(.\type ("n")) transistor_2 (.in(1'b1), .out(transistor_2_out), .gate(in_1));
  Transistor #(.\type ("n")) transistor_3 (.in(transistor_2_out), .out(out_3), .gate(in_2));
  Transistor transistor_4 (.in(1'b0), .out(out_3), .gate(in_1));

  // Notes on the sheet:
  //   傅申_PB20000051
endmodule

module Or_Gate (
  input  in_1,
  input  in_2,
  output out_3
);

  wire transistor_3_out;

  Transistor #(.\type ("n")) transistor_1 (.in(1'b1), .out(out_3), .gate(in_1));
  Transistor transistor_2 (.in(transistor_3_out), .out(out_3), .gate(in_2));
  Transistor transistor_3 (.in(1'b0), .out(transistor_3_out), .gate(in_1));
  Transistor #(.\type ("n")) transistor_4 (.in(1'b1), .out(out_3), .gate(in_2));

  // Notes on the sheet:
  //   傅申_PB20000051
endmodule

module Not_Gate (
  input  in_1,
  output out_2
);

  Transistor transistor_1 (.in(1'b1), .out(out_2), .gate(in_1));
  Transistor #(.\type ("n")) transistor_2 (.in(1'b0), .out(out_2), .gate(in_1));

  // Notes on the sheet:
  //   傅申_PB20000051
endmodule

module Nand_Gate (
  input  in_1,
  input  in_2,
  output out_3
);

  wire transistor_4_out;

  Transistor transistor_1 (.in(1'b1), .out(out_3), .gate(in_1));
  Transistor transistor_2 (.in(1'b1), .out(out_3), .gate(in_2));
  Transistor #(.\type ("n")) transistor_3 (.in(transistor_4_out), .out(out_3), .gate(in_1));
  Transistor #(.\type ("n")) transistor_4 (.in(1'b0), .out(transistor_4_out), .gate(in_2));

  // Notes on the sheet:
  //   傅申_PB20000051
endmodule

module Nor_Gate (
  input  in_1,
  input  in_2,
  output out_3
);

  wire transistor_2_out;

  Transistor #(.\type ("n")) transistor_1 (.in(1'b0), .out(out_3), .gate(in_2));
  Transistor transistor_2 (.in(1'b1), .out(transistor_2_out), .gate(in_1));
  Transistor transistor_3 (.in(transistor_2_out), .out(out_3), .gate(in_2));
  Transistor #(.\type ("n")) transistor_4 (.in(1'b0), .out(out_3), .gate(in_1));

  // Notes on the sheet:
  //   傅申_PB20000051
endmodule

module _1_bit_2_to_1_Selector (
  input  in_1,
  input  in_2,
  input  in_3,
  output out_4
);

  wire and_1_out_3, and_2_out_3, not_1_out_2;

  Not_Gate not_1 (.in_1(in_1), .out_2(not_1_out_2));
  And_Gate and_1 (.in_1(not_1_out_2), .in_2(in_2), .out_3(and_1_out_3));
  And_Gate and_2 (.in_1(in_1), .in_2(in_3), .out_3(and_2_out_3));
  Or_Gate or_1 (.in_1(and_1_out_3), .in_2(and_2_out_3), .out_3(out_4));
endmodule

module _1_bit_4_to_1_Selector (
  input  [1:0] in_1,
  input  in_2,
  input  in_3,
  input  in_4,
  input  in_5,
  output out_6
);

  wire and_1_out_3, and_2_out_3, and_3_out_3, and_4_out_3, and_5_out_3, and_6_out_3, and_7_out_3,
       and_8_out_3, not_1_out_2, not_2_out_2, or_1_out_3, or_2_out_3;

  Not_Gate not_1 (.in_1(in_1[1]), .out_2(not_1_out_2));
  Not_Gate not_2 (.in_1(in_1[0]), .out_2(not_2_out_2));
  And_Gate and_1 (.in_1(not_1_out_2), .in_2(in_2), .out_3(and_1_out_3));
  And_Gate and_2 (.in_1(not_1_out_2), .in_2(in_3), .out_3(and_2_out_3));
  And_Gate and_3 (.in_1(in_1[1]), .in_2(in_4), .out_3(and_3_out_3));
  And_Gate and_4 (.in_1(in_1[1]), .in_2(in_5), .out_3(and_4_out_3));
  And_Gate and_5 (.in_1(not_2_out_2), .in_2(and_1_out_3), .out_3(and_5_out_3));
  And_Gate and_6 (.in_1(in_1[0]), .in_2(and_2_out_3), .out_3(and_6_out_3));
  And_Gate and_7 (.in_1(not_2_out_2), .in_2(and_3_out_3), .out_3(and_7_out_3));
  And_Gate and_8 (.in_1(in_1[0]), .in_2(and_4_out_3), .out_3(and_8_out_3));
  Or_Gate or_1 (.in_1(and_5_out_3), .in_2(and_6_out_3), .out_3(or_1_out_3));
  Or_Gate or_2 (.in_1(and_7_out_3), .in_2(and_8_out_3), .out_3(or_2_out_3));
  Or_Gate or_3 (.in_1(or_1_out_3), .in_2(or_2_out_3), .out_3(out_6));
endmodule

module _2_bit_4_to_1_Selector (
  input  [1:0] in_1,
  input  [1:0] in_2,
  input  [1:0] in_3,
  input  [1:0] in_4,
  input  [1:0] in_5,
  output [1:0] out_6
);

  _1_bit_4_to_1_Selector u_1_bit_4_to_1_selector_1 (
    .in_2(in_2[0]), .in_3(in_3[0]), .in_4(in_4[0]), .in_5(in_5[0]), .out_6(out_6[0]), .in_1(in_1));
  _1_bit_4_to_1_Selector u_1_bit_4_to_1_selector_2 (
    .in_2(in_2[1]), .in_3(in_3[1]), .in_4(in_4[1]), .in_5(in_5[1]), .out_6(out_6[1]), .in_1(in_1));
endmodule
