// Logisim project circuit.circ as structural Verilog: 9 circuits, main circuit Prob 1.
module Step_1 (
  input  I4,
  input  I3,
  input  I2,
  input  I1,
  output O4,
  output O3,
  output O2,
  output O1
);

  wire and_2_out, not_2_out, not_3_out;

  not not_1 (O4, I2);
  and and_1 (O3, I2, I1);
  not not_2 (not_2_out, I1);
  not not_3 (not_3_out, I4);
  and and_2 (and_2_out, not_3_out, I2);
  or or_1 (O1, not_2_out, and_2_out);

  assign O2 = 1'b1;

  // Notes on the sheet:
  //   傅申_PB20000051
endmodule

module Step_2 (
  input  i7,
  input  i6,
  input  i5,
  input  i4,
  input  i3,
  input  i2,
  input  i1,
  input  i0,
  output y2,
  output y1,
  output y0
);

  wire and_1_out, and_2_out, and_3_out, and_4_out, and_5_out, and_6_out, and_7_out, and_8_out, and_9_out,
       not_1_out, not_2_out, not_3_out, not_4_out, not_5_out, not_6_out, not_7_out, not_8_out, not_9_out,
       not_10_out, not_11_out, not_12_out, not_13_out, not_14_out, not_15_out, not_16_out, not_17_out,
       not_18_out, not_19_out, not_20_out, not_21_out, not_22_out, not_23_out, not_24_out, not_25_out,
       not_26_out, not_27_out, not_28_out;

  not not_1 (not_1_out, i7);
  not not_2 (not_2_out, i7);
  not not_3 (not_3_out, i6);
  not not_4 (not_4_out, i7);
  not not_5 (not_5_out, i6);
  not not_6 (not_6_out, i5);
  not not_7 (not_7_out, i7);
  not not_8 (not_8_out, i7);
  not not_9 (not_9_out, i6);
  not not_10 (not_10_out, i5);
  not not_11 (not_11_out, i4);
  not not_12 (not_12_out, i7);
  not not_13 (not_13_out, i6);
  not not_14 (not_14_out, i5);
  not not_15 (not_15_out, i4);
  not not_16 (not_16_out, i3);
  not not_17 (not_17_out, i7);
  not not_18 (not_18_out, i6);
  not not_19 (not_19_out, i7);
  not not_20 (not_20_out, i6);
  not not_21 (not_21_out, i5);
  not not_22 (not_22_out, i4);
  not not_23 (not_23_out, i7);
  not not_24 (not_24_out, i6);
  not not_25 (not_25_out, i5);
  not not_26 (not_26_out, i4);
  not not_27 (not_27_out, i3);
  not not_28 (not_28_out, i2);
  and and_1 (and_1_out, not_1_out, i6);
  and and_2 (and_2_out, not_2_out, not_3_out, i5);
  and and_3 (and_3_out, not_4_out, not_5_out, not_6_out, i4);
  and and_4 (and_4_out, not_7_out, i6);
  and and_5 (and_5_out, not_8_out, not_9_out, not_10_out, not_11_out, i3);
  and and_6 (and_6_out, not_12_out, not_13_out, not_14_out, not_15_out, not_16_out, i2);
  and and_7 (and_7_out, not_17_out, not_18_out, i5);
  and and_8 (and_8_out, not_19_out, not_20_out, not_21_out, not_22_out, i3);
  and and_9 (and_9_out, not_23_out, not_24_out, not_25_out, not_26_out, not_27_out, not_28_out, i1);
  or or_1 (y2, i7, and_1_out, and_2_out, and_3_out);
  or or_2 (y1, i7, and_4_out, and_5_out, and_6_out);
  or or_3 (y0, i7, and_7_out, and_8_out, and_9_out);

  // Notes on the sheet:
  //   傅申_PB20000051
endmodule

module Step_2_minimized1 (
  input  i7,
  input  i6,
  input  i5,
  input  i4,
  input  i3,
  input  i2,
  input  i1,
  input  i0,
  output y2,
  output y1,
  output y0
);

  wire and_1_out, and_2_out, and_3_out, and_4_out, and_5_out, not_1_out, not_2_out, not_3_out, not_4_out,
       not_5_out, not_6_out, not_7_out, not_8_out, not_9_out, not_10_out;

  or or_1 (y2, i4, i5, i6, i7);
  not not_1 (not_1_out, i5);
  and and_1 (and_1_out, not_1_out, not_2_out, i2);
  not not_2 (not_2_out, i4);
  not not_3 (not_3_out, i5);
  not not_4 (not_4_out, i4);
  and and_2 (and_2_out, not_3_out, not_4_out, i3);
  not not_5 (not_5_out, i6);
  not not_6 (not_6_out, i4);
  not not_7 (not_7_out, i2);
  not not_8 (not_8_out, i6);
  not not_9 (not_9_out, i4);
  not not_10 (not_10_out, i6);
  or or_2 (y1, and_1_out, and_2_out, i6, i7);
  and and_3 (and_3_out, not_5_out, not_6_out, not_7_out, i1);
  and and_4 (and_4_out, not_8_out, not_9_out, i3);
  and and_5 (and_5_out, not_10_out, i5);
  or or_3 (y0, and_3_out, and_4_out, and_5_out, i7);

  // Notes on the sheet:
  //   傅申_PB20000051
endmodule

module Step_2_minimized2 (
  input  i7,
  input  i6,
  input  i5,
  input  i4,
  input  i3,
  input  i2,
  input  i1,
  input  i0,
  output y2,
  output y1,
  output y0
);

  wire not_1_out, not_2_out, not_3_out, not_4_out, not_5_out, or_2_out, or_3_out, or_4_out, or_5_out,
       or_6_out, or_7_out, or_8_out;

  or or_1 (y2, i7, i6, i5, i4);
  or or_2 (or_2_out, i7, i6, i3, i2);
  or or_3 (or_3_out, i7, i6, not_1_out);
  not not_1 (not_1_out, i4);
  or or_4 (or_4_out, i7, i6, not_2_out);
  not not_2 (not_2_out, i5);
  not not_3 (not_3_out, i2);
  not not_4 (not_4_out, i4);
  not not_5 (not_5_out, i6);
  and and_1 (y1, or_2_out, or_3_out, or_4_out);
  or or_5 (or_5_out, i7, i5, i3, i1);
  or or_6 (or_6_out, i7, i5, i3, not_3_out);
  or or_7 (or_7_out, i7, i5, not_4_out);
  or or_8 (or_8_out, i7, not_5_out);
  and and_2 (y0, or_5_out, or_6_out, or_7_out, or_8_out);

  // Notes on the sheet:
  //   傅申_PB20000051
endmodule

module Prob_1 (
  input  Ci1,
  input  Ai,
  input  Bi,
  output Si,
  output Ci
);

  wire and_1_out, and_2_out, and_3_out, and_4_out, and_5_out, and_6_out, and_7_out, not_1_out, not_2_out,
       not_3_out, not_4_out, not_5_out, not_6_out;

  not not_1 (not_1_out, Ci1);
  not not_2 (not_2_out, Ai);
  not not_3 (not_3_out, Ci1);
  not not_4 (not_4_out, Bi);
  not not_5 (not_5_out, Ai);
  not not_6 (not_6_out, Bi);
  and and_1 (and_1_out, Ai, Bi);
  and and_2 (and_2_out, Ci1, Bi);
  and and_3 (and_3_out, Ci1, Ai);
  and and_4 (and_4_out, not_1_out, not_2_out, Bi);
  and and_5 (and_5_out, not_3_out, Ai, not_4_out);
  and and_6 (and_6_out, Ci1, not_5_out, not_6_out);
  and and_7 (and_7_out, Ci1, Ai, Bi);
  or or_1 (Ci, and_1_out, and_2_out, and_3_out);
  or or_2 (Si, and_4_out, and_5_out, and_6_out, and_7_out);

  // Notes on the sheet:
  //   傅申_PB20000051
endmodule

module Prob_2 (
  input  G1,
  input  G2,
  input  G3,
  input  A2,
  input  A1,
  input  A0,
  output Y7,
  output Y6,
  output Y5,
  output Y4,
  output Y3,
  output Y2,
  output Y1,
  output Y0
);

  wire not_1_out, not_2_out, not_3_out, not_4_out, not_5_out, not_6_out, not_7_out, not_8_out, not_9_out,
       not_10_out, not_11_out, not_12_out, not_13_out, not_14_out, not_15_out, not_16_out, not_17_out,
       not_18_out, not_19_out, not_20_out;

  not not_1 (not_1_out, G1);
  not not_2 (not_2_out, A2);
  not not_3 (not_3_out, A1);
  not not_4 (not_4_out, A0);
  not not_5 (not_5_out, G1);
  not not_6 (not_6_out, A2);
  not not_7 (not_7_out, A1);
  not not_8 (not_8_out, G1);
  not not_9 (not_9_out, A2);
  not not_10 (not_10_out, A0);
  not not_11 (not_11_out, G1);
  not not_12 (not_12_out, A2);
  not not_13 (not_13_out, G1);
  not not_14 (not_14_out, A1);
  not not_15 (not_15_out, A0);
  not not_16 (not_16_out, G1);
  not not_17 (not_17_out, A1);
  not not_18 (not_18_out, G1);
  not not_19 (not_19_out, A0);
  not not_20 (not_20_out, G1);
  or or_1 (Y7, not_1_out, G2, G3, not_2_out, not_3_out, not_4_out);
  or or_2 (Y6, not_5_out, G2, G3, not_6_out, not_7_out, A0);
  or or_3 (Y5, not_8_out, G2, G3, not_9_out, A1, not_10_out);
  or or_4 (Y4, not_11_out, G2, G3, not_12_out, A1, A0);
  or or_5 (Y3, not_13_out, G2, G3, A2, not_14_out, not_15_out);
  or or_6 (Y2, not_16_out, G2, G3, A2, not_17_out, A0);
  or or_7 (Y1, not_18_out, not_19_out, A1, A2, G3, G2);
  or or_8 (Y0, not_20_out, G2, G3, A2, A1, A0);

  // Notes on the sheet:
  //   傅申_PB20000051
endmodule

module Prob_3 (
  input  sel,
  input  a,
  input  b,
  output out
);

  wire and_1_out, and_2_out, not_1_out;

  not not_1 (not_1_out, sel);
  and and_1 (and_1_out, not_1_out, a);
  and and_2 (and_2_out, sel, b);
  or or_1 (out, and_1_out, and_2_out);

  // Notes on the sheet:
  //   傅申_PB20000051
endmodule

module Prob_4 (
  input  sel1,
  input  sel0,
  input  a,
  input  b,
  input  c,
  input  d,
  output out
);

  wire prob_3_1_out, prob_3_2_out;

  Prob_3 prob_3_1 (.a(a), .b(c), .out(prob_3_1_out), .sel(sel1));
  Prob_3 prob_3_2 (.a(b), .b(d), .out(prob_3_2_out), .sel(sel1));
  Prob_3 prob_3_3 (.a(prob_3_1_out), .b(prob_3_2_out), .out(out), .sel(sel0));

  // Notes on the sheet:
  //   傅申_PB20000051
  //   low_bit_0
  //   low_bit_1
endmodule

module Prob_6 (
  input  a,
  input  b,
  input  c,
  output S1,
  output S2
);

  wire xor_1_out;

  xor xor_1 (xor_1_out, a, b);
  xor xor_2 (S1, xor_1_out, c);
  not not_1 (S2, S1);

  // Notes on the sheet:
  //   傅申_PB20000051
endmodule
