// Logisim project probs_cir.circ as structural Verilog: 13 circuits, main circuit prob.1.RS_Latch
module prob_1_RS_Latch (
  input  R,
  input  S,
  output Q,
  output nQ
);

  nand nand_1 (Q, R, nQ);
  nand nand_2 (nQ, Q, S);

  // Notes on the sheet:
  //   傅申_PB20000051
endmodule

module prob_1_2 (
  input  R,
  input  R_2,
  input  S,
  input  S_2,
  input  R_3,
  input  R_4,
  input  S_3,
  input  S_4,
  output Q,
  output Q_2,
  output nQ,
  output nQ_2,
  output Q_3,
  output Q_4,
  output nQ_3,
  output nQ_4
);

  nand nand_1 (Q, R, nQ);
  nand nand_2 (nQ, Q, S);
  nand nand_3 (Q_3, R_3, nQ_3);
  nand nand_4 (nQ_3, Q_3, S_3);
  nand nand_5 (Q_2, R_2, nQ_2);
  nand nand_6 (nQ_2, Q_2, S_2);
  nand nand_7 (Q_4, R_4, nQ_4);
  nand nand_8 (nQ_4, Q_4, S_4);

  // Notes on the sheet:
  //   傅申_PB20000051
endmodule

module prob_2_1_D_Latch (
  input  CLK,
  input  D,
  output Q,
  output nQ
);

  wire and_1_out, and_2_out, not_1_out;

  not not_1 (not_1_out, D);
  and and_1 (and_1_out, CLK, not_1_out);
  and and_2 (and_2_out, CLK, D);
  nor nor_1 (Q, and_1_out, nQ);
  nor nor_2 (nQ, Q, and_2_out);

  // Notes on the sheet:
  //   傅申_PB20000051
endmodule

module \prob_2_2_同步置位D触发器  (
  input  CLK,
  input  D,
  input  nST,
  output Q,
  output nQ
);

  wire not_1_out, not_2_out, or_1_out, prob_2_1_d_latch_1_q;

  not not_1 (not_1_out, nST);
  not not_2 (not_2_out, CLK);
  or or_1 (or_1_out, D, not_1_out);
  prob_2_1_D_Latch prob_2_1_d_latch_1 (.CLK(not_2_out), .D(or_1_out), .Q(prob_2_1_d_latch_1_q));  // open: nQ
  prob_2_1_D_Latch prob_2_1_d_latch_2 (.CLK(CLK), .D(prob_2_1_d_latch_1_q), .Q(Q), .nQ(nQ));

  // Notes on the sheet:
  //   傅申_PB20000051
endmodule

module prob_2_3 (
  input  in_1,
  input  in_2,
  output out_3,
  output out_4
);

  wire clock_1_out;

  Clock clock_1 (.out(clock_1_out));
  \prob_2_2_同步置位D触发器  \prob_2_2_同步置位d触发器_1  (.CLK(clock_1_out), .D(in_1), .nST(in_2), .Q(out_3), .nQ(out_4));
endmodule

module SR_Latch (
  input  R,
  input  S,
  output Q,
  output nQ
);

  nor nor_1 (Q, R, nQ);
  nor nor_2 (nQ, Q, S);
endmodule

module prob_3_framework (
  input  CLK,
  input  D,
  input  nRST,
  output Q,
  output nQ
);

  wire and_1_out, and_2_out, not_1_out, not_2_out, or_1_out, or_2_out;

  not not_1 (not_1_out, nRST);
  buf or_1 (or_1_out, not_1_out);  // OR_Gate
  buf and_1 (and_1_out, nRST);  // AND_Gate
  SR_Latch sr_latch_1 (.R(or_1_out), .S(and_1_out));  // open: Q, nQ
  not not_2 (not_2_out, nRST);
  buf or_2 (or_2_out, not_2_out);  // OR_Gate
  buf and_2 (and_2_out, nRST);  // AND_Gate
  SR_Latch sr_latch_2 (.R(or_2_out), .S(and_2_out), .Q(Q), .nQ(nQ));
endmodule

module \prob_3_1_异步复位D触发器  (
  input  CLK,
  input  D,
  input  nRST,
  output Q,
  output nQ
);

  wire and_1_out, and_2_out, and_3_out, and_4_out, and_5_out, and_6_out, not_1_out, not_2_out, not_3_out,
       not_4_out, or_1_out, or_2_out, sr_latch_1_nq, sr_latch_1_q;

  not not_1 (not_1_out, CLK);
  not not_2 (not_2_out, D);
  and and_1 (and_1_out, not_1_out, not_2_out);
  not not_3 (not_3_out, nRST);
  and and_2 (and_2_out, not_1_out, D);
  or or_1 (or_1_out, and_1_out, not_3_out);
  and and_3 (and_3_out, nRST, and_2_out);
  SR_Latch sr_latch_1 (.R(or_1_out), .S(and_3_out), .Q(sr_latch_1_q), .nQ(sr_latch_1_nq));
  and and_4 (and_4_out, CLK, sr_latch_1_q);
  and and_5 (and_5_out, CLK, sr_latch_1_nq);
  or or_2 (or_2_out, and_5_out, not_4_out);
  not not_4 (not_4_out, nRST);
  and and_6 (and_6_out, and_4_out, nRST);
  SR_Latch sr_latch_2 (.R(or_2_out), .S(and_6_out), .Q(Q), .nQ(nQ));

  // Notes on the sheet:
  //   傅申_PB20000051
endmodule

module \prob_3_2_递增计数器  (
  input  CLK,
  input  nRST,
  output [3:0] CNT
);

  wire [3:0] adder_1_out;

  Adder #(.width(4)) adder_1 (.a(CNT), .b(4'b0001), .out(adder_1_out), .cin(1'b0));  // open: cout
  \prob_3_1_异步复位D触发器  \prob_3_1_异步复位d触发器_1  (.CLK(CLK), .D(adder_1_out[0]), .nRST(nRST), .Q(CNT[0]));  // open: nQ
  \prob_3_1_异步复位D触发器  \prob_3_1_异步复位d触发器_2  (.CLK(CLK), .D(adder_1_out[1]), .nRST(nRST), .Q(CNT[1]));  // open: nQ
  \prob_3_1_异步复位D触发器  \prob_3_1_异步复位d触发器_3  (.CLK(CLK), .D(adder_1_out[2]), .nRST(nRST), .Q(CNT[2]));  // open: nQ
  \prob_3_1_异步复位D触发器  \prob_3_1_异步复位d触发器_4  (.CLK(CLK), .D(adder_1_out[3]), .nRST(nRST), .Q(CNT[3]));  // open: nQ

  // Notes on the sheet:
  //   傅申_PB20000051
endmodule

module \prob_4_1_异步置位D触发器  (
  input  CLK,
  input  D,
  input  nST,
  output Q,
  output nQ
);

  wire and_1_out, and_2_out, and_3_out, and_4_out, and_5_out, and_6_out, not_1_out, not_2_out, not_3_out,
       not_4_out, or_1_out, or_2_out, sr_latch_1_nq, sr_latch_1_q;

  not not_1 (not_1_out, CLK);
  not not_2 (not_2_out, D);
  and and_1 (and_1_out, not_1_out, not_2_out);
  not not_3 (not_3_out, nST);
  and and_2 (and_2_out, not_1_out, D);
  and and_3 (and_3_out, and_1_out, nST);
  or or_1 (or_1_out, not_3_out, and_2_out);
  SR_Latch sr_latch_1 (.R(and_3_out), .S(or_1_out), .Q(sr_latch_1_q), .nQ(sr_latch_1_nq));
  and and_4 (and_4_out, CLK, sr_latch_1_q);
  and and_5 (and_5_out, CLK, sr_latch_1_nq);
  and and_6 (and_6_out, and_5_out, nST);
  or or_2 (or_2_out, and_4_out, not_4_out);
  not not_4 (not_4_out, nST);
  SR_Latch sr_latch_2 (.R(and_6_out), .S(or_2_out), .Q(Q), .nQ(nQ));

  // Notes on the sheet:
  //   傅申_PB20000051
endmodule

module \prob_4_2_自减器  (
  input  [3:0] in_1,
  output [3:0] \傅申_PB20000051 
);

  wire and_1_out, and_2_out, and_3_out, and_4_out, and_5_out, not_2_out, not_3_out, not_4_out, or_2_out,
       or_3_out, or_5_out;

  and and_1 (and_1_out, in_1[0], in_1[1]);
  not not_1 (\傅申_PB20000051 [0], in_1[0]);
  not not_2 (not_2_out, or_2_out);
  and and_2 (and_2_out, not_2_out, in_1[2]);
  or or_1 (\傅申_PB20000051 [1], and_1_out, and_4_out, and_2_out);
  or or_2 (or_2_out, in_1[1], in_1[0]);
  or or_3 (or_3_out, or_2_out, or_5_out);
  and and_3 (and_3_out, or_2_out, in_1[2]);
  or or_4 (\傅申_PB20000051 [2], and_3_out, and_4_out);
  or or_5 (or_5_out, in_1[2], in_1[3]);
  not not_3 (not_3_out, in_1[0]);
  and and_4 (and_4_out, in_1[3], not_3_out);
  not not_4 (not_4_out, or_3_out);
  or or_6 (\傅申_PB20000051 [3], not_4_out, and_5_out);
  and and_5 (and_5_out, in_1[3], in_1[0]);
endmodule

module \prob_4_3_递减计数器  (
  input  CLK,
  input  nRST,
  output [3:0] CNT
);

  wire [3:0] \prob_4_2_自减器_1_傅申_pb20000051 ;

  \prob_4_2_自减器  \prob_4_2_自减器_1  (.in_1(CNT), .\傅申_PB20000051 (\prob_4_2_自减器_1_傅申_pb20000051 ));
  \prob_4_1_异步置位D触发器  \prob_4_1_异步置位d触发器_1  (
    .D(\prob_4_2_自减器_1_傅申_pb20000051 [0]), .nST(nRST), .Q(CNT[0]), .CLK(CLK));  // open: nQ
  \prob_3_1_异步复位D触发器  \prob_3_1_异步复位d触发器_1  (
    .CLK(CLK), .D(\prob_4_2_自减器_1_傅申_pb20000051 [1]), .nRST(nRST), .Q(CNT[1]));  // open: nQ
  \prob_3_1_异步复位D触发器  \prob_3_1_异步复位d触发器_2  (
    .CLK(CLK), .D(\prob_4_2_自减器_1_傅申_pb20000051 [2]), .nRST(nRST), .Q(CNT[2]));  // open: nQ
  \prob_4_1_异步置位D触发器  \prob_4_1_异步置位d触发器_2  (
    .D(\prob_4_2_自减器_1_傅申_pb20000051 [3]), .nST(nRST), .Q(CNT[3]), .CLK(CLK));  // open: nQ

  // Notes on the sheet:
  //   傅申_PB20000051
endmodule

module prob_5_1_3_1 (
  input  CLK,
  input  D,
  input  RST,
  output Q,
  output nQ
);

  wire and_1_out, and_2_out, and_3_out, and_4_out, and_5_out, and_6_out, not_1_out, not_2_out, not_3_out,
       not_4_out, not_5_out, or_1_out, or_2_out, sr_latch_1_q;

  not not_1 (not_1_out, CLK);
  not not_2 (not_2_out, D);
  and and_1 (and_1_out, not_1_out, not_2_out);
  and and_2 (and_2_out, not_1_out, D);
  not not_3 (not_3_out, RST);
  or or_1 (or_1_out, and_1_out, RST);
  and and_3 (and_3_out, not_3_out, and_2_out);
  SR_Latch sr_latch_1 (.R(or_1_out), .S(and_3_out), .Q(sr_latch_1_q));  // open: nQ
  and and_4 (and_4_out, CLK, sr_latch_1_q);
  and and_5 (and_5_out, CLK, not_4_out);
  not not_4 (not_4_out, sr_latch_1_q);
  not not_5 (not_5_out, RST);
  or or_2 (or_2_out, and_5_out, RST);
  and and_6 (and_6_out, and_4_out, not_5_out);
  SR_Latch sr_latch_2 (.R(or_2_out), .S(and_6_out), .Q(Q), .nQ(nQ));
endmodule
