// Logisim project steps_cir.circ as structural Verilog: 10 circuits, main circuit step.1.
module step_1 (
  input  in_1,
  input  in_2,
  output out_3,
  output out_4,
  output out_5,
  output out_6
);

  not not_1 (out_3, out_5);
  not not_2 (out_5, out_3);
  not not_3 (out_4, out_6);
  not not_4 (out_6, out_4);

  // Notes on the sheet:
  //   傅申_PB20000051
endmodule

module step_2 (
  input  R,
  input  R_2,
  input  S,
  input  S_2,
  input  R_3,
  input  R_4,
  input  S_3,
  input  S_4,
  output Q,
  output Q_2,
  output nQ,
  output nQ_2,
  output Q_3,
  output Q_4,
  output nQ_3,
  output nQ_4
);

  nor nor_1 (Q, R, nQ);
  nor nor_2 (nQ, Q, S);
  nor nor_3 (Q_3, R_3, nQ_3);
  nor nor_4 (nQ_3, Q_3, S_3);
  nor nor_5 (Q_2, R_2, nQ_2);
  nor nor_6 (nQ_2, Q_2, S_2);
  nor nor_7 (Q_4, R_4, nQ_4);
  nor nor_8 (nQ_4, Q_4, S_4);

  // Notes on the sheet:
  //   傅申_PB20000051
endmodule

module SR_Latch (
  input  R,
  input  S,
  output Q,
  output nQ
);

  nor nor_1 (Q, R, nQ);
  nor nor_2 (nQ, Q, S);

  // Notes on the sheet:
  //   傅申_PB20000051
endmodule

module step_3 (
  input  CLK,
  input  CLK_2,
  input  D,
  input  D_2,
  input  CLK_3,
  input  CLK_4,
  input  D_3,
  input  D_4,
  output Q,
  output Q_2,
  output nQ,
  output nQ_2,
  output Q_3,
  output Q_4,
  output nQ_3,
  output nQ_4
);

  wire and_1_out, and_2_out, and_3_out, and_4_out, and_5_out, and_6_out, and_7_out, and_8_out, not_1_out,
       not_2_out, not_3_out, not_4_out;

  not not_1 (not_1_out, D);
  not not_2 (not_2_out, D_3);
  and and_1 (and_1_out, CLK, not_1_out);
  and and_2 (and_2_out, CLK, D);
  and and_3 (and_3_out, CLK_3, not_2_out);
  and and_4 (and_4_out, CLK_3, D_3);
  SR_Latch sr_latch_1 (.R(and_1_out), .S(and_2_out), .Q(Q), .nQ(nQ));
  SR_Latch sr_latch_2 (.R(and_3_out), .S(and_4_out), .Q(Q_3), .nQ(nQ_3));
  not not_3 (not_3_out, D_2);
  not not_4 (not_4_out, D_4);
  and and_5 (and_5_out, CLK_2, not_3_out);
  and and_6 (and_6_out, CLK_2, D_2);
  and and_7 (and_7_out, CLK_4, not_4_out);
  and and_8 (and_8_out, CLK_4, D_4);
  SR_Latch sr_latch_3 (.R(and_5_out), .S(and_6_out), .Q(Q_2), .nQ(nQ_2));
  SR_Latch sr_latch_4 (.R(and_7_out), .S(and_8_out), .Q(Q_4), .nQ(nQ_4));

  // Notes on the sheet:
  //   傅申_PB20000051
  //   跟随
  //   锁存
endmodule

module D_Latch (
  input  CLK,
  input  D,
  output Q,
  output nQ
);

  wire and_1_out, and_2_out, not_1_out;

  not not_1 (not_1_out, D);
  and and_1 (and_1_out, CLK, not_1_out);
  and and_2 (and_2_out, CLK, D);
  SR_Latch sr_latch_1 (.R(and_1_out), .S(and_2_out), .Q(Q), .nQ(nQ));

  // Notes on the sheet:
  //   傅申_PB20000051
endmodule

module step_4 (
  input  D,
  input  D_2,
  input  nRST,
  output Q,
  output nQ,
  output Q_2,
  output nQ_2
);

  wire and_1_out, CLK_2_out, CLK_out, d_latch_1_q, not_1_out;

  Clock CLK (.out(CLK_out));
  not not_1 (not_1_out, CLK_out);
  Clock CLK_2 (.out(CLK_2_out));
  D_Latch d_latch_1 (.CLK(not_1_out), .D(D), .Q(d_latch_1_q));  // open: nQ
  and and_1 (and_1_out, D_2, nRST);
  D_Filp_Flop d_filp_flop_1 (.CLK(CLK_2_out), .D(and_1_out), .Q(Q_2), .nQ(nQ_2));
  D_Latch d_latch_2 (.CLK(CLK_out), .D(d_latch_1_q), .Q(Q), .nQ(nQ));

  // Notes on the sheet:
  //   D1
  //   傅申_PB20000051
  //   傅申_PB20000051
  //   D2
endmodule

module D_Filp_Flop (
  input  CLK,
  input  D,
  output Q,
  output nQ
);

  wire d_latch_1_q, not_1_out;

  not not_1 (not_1_out, CLK);
  D_Latch d_latch_1 (.CLK(not_1_out), .D(D), .Q(d_latch_1_q));  // open: nQ
  D_Latch d_latch_2 (.CLK(CLK), .D(d_latch_1_q), .Q(Q), .nQ(nQ));

  // Notes on the sheet:
  //   D1
  //   傅申_PB20000051
  //   D2
endmodule

module step_5 (
  input  [3:0] D_IN,
  input  nRST,
  input  [3:0] D_IN_2,
  input  nRST_2,
  output [3:0] out_5,
  output [3:0] out_6
);

  wire and_1_out, and_2_out, and_3_out, and_4_out, and_5_out, and_6_out, and_7_out, and_8_out, CLK_2_out,
       CLK_out, d_filp_flop_5_q, d_filp_flop_6_q, not_1_out, not_2_out;

  Clock CLK (.out(CLK_out));
  Clock CLK_2 (.out(CLK_2_out));
  not not_1 (not_1_out, D_IN_2[0]);
  not not_2 (not_2_out, D_IN_2[1]);
  and and_1 (and_1_out, D_IN[0], nRST);
  and and_2 (and_2_out, D_IN[1], nRST);
  and and_3 (and_3_out, D_IN[2], nRST);
  and and_4 (and_4_out, D_IN[3], nRST);
  and and_5 (and_5_out, not_1_out, nRST_2);
  and and_6 (and_6_out, not_2_out, nRST_2);
  and and_7 (and_7_out, D_IN_2[2], nRST_2);
  and and_8 (and_8_out, D_IN_2[3], nRST_2);
  D_Filp_Flop d_filp_flop_1 (.CLK(CLK_out), .D(and_1_out), .Q(out_5[0]));  // open: nQ
  D_Filp_Flop d_filp_flop_2 (.CLK(CLK_out), .D(and_2_out), .Q(out_5[1]));  // open: nQ
  D_Filp_Flop d_filp_flop_3 (.CLK(CLK_out), .D(and_3_out), .Q(out_5[2]));  // open: nQ
  D_Filp_Flop d_filp_flop_4 (.CLK(CLK_out), .D(and_4_out), .Q(out_5[3]));  // open: nQ
  D_Filp_Flop d_filp_flop_5 (.CLK(CLK_2_out), .D(and_5_out), .Q(d_filp_flop_5_q));  // open: nQ
  D_Filp_Flop d_filp_flop_6 (.CLK(CLK_2_out), .D(and_6_out), .Q(d_filp_flop_6_q));  // open: nQ
  D_Filp_Flop d_filp_flop_7 (.CLK(CLK_2_out), .D(and_7_out), .Q(out_6[2]));  // open: nQ
  D_Filp_Flop d_filp_flop_8 (.CLK(CLK_2_out), .D(and_8_out), .Q(out_6[3]));  // open: nQ
  not not_3 (out_6[0], d_filp_flop_5_q);
  not not_4 (out_6[1], d_filp_flop_6_q);

  // Notes on the sheet:
  //   傅申_PB20000051
  //   傅申_PB20000051
endmodule

module REG4 (
  input  [3:0] D_IN,
  input  CLK,
  input  nRST,
  output [3:0] out_4
);

  wire and_1_out, and_2_out, and_3_out, and_4_out;

  and and_1 (and_1_out, D_IN[0], nRST);
  and and_2 (and_2_out, D_IN[1], nRST);
  and and_3 (and_3_out, D_IN[2], nRST);
  and and_4 (and_4_out, D_IN[3], nRST);
  D_Filp_Flop d_filp_flop_1 (.CLK(CLK), .D(and_1_out), .Q(out_4[0]));  // open: nQ
  D_Filp_Flop d_filp_flop_2 (.CLK(CLK), .D(and_2_out), .Q(out_4[1]));  // open: nQ
  D_Filp_Flop d_filp_flop_3 (.CLK(CLK), .D(and_3_out), .Q(out_4[2]));  // open: nQ
  D_Filp_Flop d_filp_flop_4 (.CLK(CLK), .D(and_4_out), .Q(out_4[3]));  // open: nQ

  // Notes on the sheet:
  //   傅申_PB20000051
endmodule

module step_6 (
  input  RST,
  output [3:0] out_2
);

  wire CLK_out, not_1_out;
  wire [3:0] adder_1_out;

  Clock CLK (.out(CLK_out));
  Adder #(.width(4)) adder_1 (.a(out_2), .b(4'b0001), .out(adder_1_out), .cin(1'b0));  // open: cout
  not not_1 (not_1_out, RST);
  REG4 reg4_1 (.D_IN(adder_1_out), .CLK(CLK_out), .nRST(not_1_out), .out_4(out_2));

  // Notes on the sheet:
  //   傅申_PB20000051
endmodule
