// Logisim project Prob.2.circ as structural Verilog: 2 circuits, main circuit main
module main (
  input  sw,
  input  rst,
  output [3:0] cnt
);

  wire clk_out, d_ff_1_q, d_ff_2_q, not_1_out, xnor_1_out;
  wire [3:0] adder_1_out;

  Clock clk (.out(clk_out));
  D_Flip_Flop d_ff_1 (.clk(clk_out), .D(sw), .Q(d_ff_1_q));  // open: Qn, preset, en, reset
  D_Flip_Flop d_ff_2 (.clk(clk_out), .D(d_ff_1_q), .Q(d_ff_2_q));  // open: Qn, preset, en, reset
  not not_1 (not_1_out, d_ff_2_q);
  xnor xnor_1 (xnor_1_out, not_1_out, d_ff_1_q);
  Adder #(.width(4)) adder_1 (.a(4'b0000), .b(cnt), .out(adder_1_out), .cin(1'b1));  // open: cout
  D_Latch_4bit d_latch_4bit_1 (.D(adder_1_out), .rst(rst), .Q(cnt), .clk(xnor_1_out));

  // Notes on the sheet:
  //   sw_edge
endmodule

module D_Latch_4bit (
  input  clk,
  input  [3:0] D,
  input  rst,
  output [3:0] Q
);

  D_Flip_Flop d_ff_1 (.clk(clk), .D(D[0]), .Q(Q[0]), .reset(rst));  // open: Qn, preset, en
  D_Flip_Flop d_ff_2 (.clk(clk), .D(D[1]), .Q(Q[1]), .reset(rst));  // open: Qn, preset, en
  D_Flip_Flop d_ff_3 (.clk(clk), .D(D[2]), .Q(Q[2]), .reset(rst));  // open: Qn, preset, en
  D_Flip_Flop d_ff_4 (.clk(clk), .D(D[3]), .Q(Q[3]), .reset(rst));  // open: Qn, preset, en
endmodule
